// Logisim project Desafio2.circ as structural Verilog: 1 circuit, main circuit main
module main (
  input  Ta,
  input  Tb,
  input  Tc
);

  wire and_1_out, and_2_out, not_1_out, not_2_out, not_3_out, not_4_out, not_5_out, not_6_out, not_7_out,
       not_8_out, not_9_out, or_1_out;

  not not_1 (not_1_out, Ta);
  not not_2 (not_2_out, Tb);
  not not_3 (not_3_out, Tb);
  not not_4 (not_4_out, Tc);
  not not_5 (not_5_out, and_1_out);
  and and_1 (and_1_out, not_1_out, not_2_out);
  and and_2 (and_2_out, not_3_out, not_4_out);
  not not_6 (not_6_out, and_2_out);
  not not_7 (not_7_out, not_5_out);
  not not_8 (not_8_out, not_6_out);
  LED led_1 (.in(not_9_out));
  or or_1 (or_1_out, not_7_out, not_8_out);
  not not_9 (not_9_out, or_1_out);

  // Notes on the sheet:
  //   S
endmodule
