// Logisim project Desafio3.circ as structural Verilog: 1 circuit, main circuit main
module main (
  input  D,
  input  C,
  input  T,
  input  F
);

  wire and_1_out, and_2_out, and_3_out, not_1_out, not_2_out, or_1_out, or_2_out;

  not not_1 (not_1_out, C);
  not not_2 (not_2_out, F);
  or or_1 (or_1_out, C, not_1_out);
  or or_2 (or_2_out, F, not_2_out);
  and and_1 (and_1_out, D, or_1_out);
  and and_2 (and_2_out, T, or_2_out);
  and and_3 (and_3_out, and_1_out, and_2_out);
  LED led_1 (.in(and_3_out));

  // Notes on the sheet:
  //   S = ( ( D. ( E + !E ) ) . ( T . ( F + !F ) ) )
  //   S = S1 . S2
  //   S
endmodule
