// Logisim project Exercicio01.circ as structural Verilog: 1 circuit, main circuit main
module main (
  input  A,
  input  B,
  input  C,
  input  D,
  input  E
);

  wire and_1_out, and_2_out, or_1_out;

  and and_1 (and_1_out, A, B, C);
  and and_2 (and_2_out, D, E);
  or or_1 (or_1_out, and_1_out, and_2_out);
  LED led_1 (.in(or_1_out));

  // Notes on the sheet:
  //   S1 = A.B.C
  //   S2 = D.E
  //   S
  //   (A.B.C) + (D.E)
endmodule
