// Logisim project Exercicio02.circ as structural Verilog: 1 circuit, main circuit main
module main (
  input  A,
  input  B,
  input  C,
  input  D,
  input  E,
  input  F
);

  wire and_1_out, and_2_out, and_3_out, or_1_out;

  and and_1 (and_1_out, A, B);
  and and_2 (and_2_out, C, D);
  and and_3 (and_3_out, E, F);
  LED led_1 (.in(or_1_out));
  or or_1 (or_1_out, and_1_out, and_2_out, and_3_out);

  // Notes on the sheet:
  //   S1
  //   S2
  //   S3
  //   S
endmodule
